# Fritzing sketch Fritzing sketch (saved by Fritzing 0.9.3b)

parts:
  Part1 = Adafruit Motor/Stepper/Servo Shield [part_number="Adafruit #1438"]
  M1 = DC Motor
  M2 = DC Motor
  LED1 = smd LED [color="Red (633nm)" package="1206 [SMD]"]  # not connected
  LED2 = smd LED [color="Red (633nm)" package="1206 [SMD]"]  # not connected
  LED3 = smd LED [color="Red (633nm)" package="1206 [SMD]"]  # not connected
  LED4 = smd LED [color="Red (633nm)" package="1206 [SMD]"]
  J2 = Infrared Proximity Sensor
  J3 = Infrared Proximity Sensor
  R1 = Resistor [tolerance=±5% resistance=220 package="1206 [SMD]"]  # not connected
  R2 = Resistor [tolerance=±5% resistance=220 package="1206 [SMD]"]  # not connected
  R3 = Resistor [tolerance=±5% resistance=220 package="1206 [SMD]"]  # not connected
  R4 = Resistor [tolerance=±5% resistance=220 package="1206 [SMD]"]
  J1 = Piezo Speaker

nets:
  N1: Part1.M2A, M1.pin_1
  N2: Part1.M2B, M1.pin_2
  N3: Part1.M1B, M2.pin_1
  N4: Part1.M1A, M2.pin_2
  GND: Part1.GND, LED4.cathode, J2.GND, J3.GND, J1.pin1
  VCC: Part1.VMOTOR, J2.Vcc, J3.Vcc
  N5: Part1.AD0, J2.Vout
  N6: Part1.AD1, J3.Vout
  N7: Part1.AD2, J1.pin2
  N8: Part1.AD3, R4.Pin_1

custom parts:
  Adafruit Motor/Stepper/Servo Shield: The original Adafruit Motorshield kit is one of our most beloved kits, which is why we decided to make something even better. We have upgraded the shield kit to make the bestest, easiest way to drive DC and Stepper motors. This shield will make quick work of your next robotics project! We kept the ability to drive up to 4 DC motors or 2 stepper motors, but added many improvements: Instead of a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
